# Fritzing sketch Destination_notifier_LED (saved by Fritzing 0.9.3b)

parts:
  Part1 = Arduino Uno (Rev3) - ICSP
  U1 = SUP500F [package=sup500f]
  LED1 = LED - 5mm [color="Red (633nm)" package="5 mm [THT]"]

nets:
  N1: Part1.D13/SCK, LED1.anode
  GND: Part1.GND, U1.GND, LED1.cathode
  N2: Part1.D3_PWM, U1.RX-I
  N3: Part1.D4, U1.TX-O
  VIN: Part1.VIN, U1.VCC
