# Fritzing sketch Destination_notifier_motor (saved by Fritzing 0.9.3b)
breadboards: 1

parts:
  Part1 = Arduino Uno (Rev3) - ICSP
  IC1 = L293D [package=THT]
  M1 = DC Motor
  U1 = SUP500F [package=sup500f]

nets:
  GND: Part1.GND, IC1.0V, U1.GND
  N1: Part1.D3_PWM, U1.RX-I
  N2: Part1.D4, U1.TX-O
  N3: Part1.D6_PWM, IC1.In_1
  N4: Part1.D7, IC1.In_2
  5V: Part1.5V, IC1.Enable_1, IC1.+Vmotor, IC1.+V, U1.VCC
  N5: IC1.Out_1_(_Controlled_by_Enable_1_), M1.pin_1
  N6: IC1.Out_2_(_Controlled_by_Enable_1_), M1.pin_2
