# Fritzing sketch Read_Lat_Lng (saved by Fritzing 0.9.3b)

parts:
  Part1 = Arduino Uno (Rev3) - ICSP
  U1 = SUP500F [package=sup500f]

nets:
  N1: Part1.D3_PWM, U1.RX-I
  N2: Part1.D4, U1.TX-O
  GND: Part1.GND, U1.GND
  VIN: Part1.VIN, U1.VCC
