# Fritzing sketch Arduino_Birthday_Candle   (saved by Fritzing 0.9.3b)
circuit board: 8.46667cm x 5.64444cm
breadboards: 1

parts:
  Part1 = Arduino Uno (Rev3) - ICSP
  FC-1 = sound sensor
  LED1 = LEDs [package=led10mm]
  R1 = Resistor [tolerance=±5% resistance=220 package="0805 [SMD]"]

nets:
  N1: Part1.GND, FC-1.connector9, R1.Pin_1
  N2: Part1.D13/SCK, LED1.A
  N3: Part1.D7, FC-1.connector10
  N4: Part1.5V, FC-1.connector8
  N5: LED1.C, R1.Pin_0
