# Fritzing sketch Circuit_Diagram (saved by Fritzing 0.9.3b)

parts:
  Scematic_Diagram = Arduino Micro (Rev3)
  IR1 = TSOP312.., 314.. [package=THT]

nets:
  N1: Scematic_Diagram.MOSI, IR1.Data
  GND: Scematic_Diagram.GND, IR1.GND
  N2: Scematic_Diagram.5V, IR1.Vs
