# Fritzing sketch Proximity_Lamp_Using_Arduino (saved by Fritzing 0.9.3b)

parts:
  Part1 = Arduino Uno (Rev3)
  LED1 = smd LED [color="White (4500K)" package="0603 [SMD]"]
  R1 = Resistor [tolerance=±5% resistance=10M package="1206 [SMD]"]

nets:
  N1: Part1.D9_PWM, LED1.anode
  N2: Part1.GND, LED1.cathode
  N3: Part1.D2, R1.Pin_1
  N4: Part1.D4, R1.Pin_0

notes:
  Here Pin 4 is sensor pin .Connect Aluminium foil to Pin 4. It act as Proximity Sensor.
