# Fritzing sketch circuit diagram (saved by Fritzing 0.9.3b)
breadboards: 1

parts:
  Pro_Micro1 = Pro Micro
  J1 = Piezo Speaker
  R1 = Resistor [tolerance=±5% resistance=1M package="0402 [SMD]"]

nets:
  N1: Pro_Micro1.D18/A0, J1.pin2, R1.Pin_1
  N2: Pro_Micro1.GND, J1.pin1, R1.Pin_0

custom parts:
  Pro Micro: The SparkFun Pro Micro is a complete USB-based microcontoller development system, in a very small footprint, capable of implementing many types of projects. All programming can be done via the USB port.
